# Fritzing sketch RearDetectFrizing (saved by Fritzing 0.9.3b)
breadboards: 1

parts:
  Raspberry_Pi1 = Raspberry Pi B+  # not connected
  부품1 = Adafruit T-Cobbler Plus [part_number="Adafruit #1989 and #2028"]
  SG1 = Buzzer 12mm [package=buzzer-ccv-kit]
  hc-sr1 = hc-sr04
  hc-sr2 = hc-sr04
  hc-sr3 = hc-sr04
  R1 = Resistor [tolerance=±5% resistance=220 package="2010 [SMD]"]
  R2 = Resistor [tolerance=±5% resistance=220 package=THT]
  R3 = Resistor [tolerance=±5% resistance=220 package=THT]
  R4 = Resistor [tolerance=±5% resistance=220 package=THT]
  R5 = Resistor [tolerance=±5% resistance=220 package=THT]
  R6 = Resistor [tolerance=±5% resistance=220 package=THT]
  S1 = H-Bridge with L298N
  VCC1 = Battery block 9V
  M2 = DC Motor
  M3 = DC Motor

nets:
  N1: 부품1.GPIO4, hc-sr1.Trig
  GND: 부품1.GND, 부품1.GPIO6, SG1.1, hc-sr1.GND, hc-sr2.GND, hc-sr3.GND, R2.Pin_1, R4.Pin_1, R6.Pin_1, S1.GND
  N2: 부품1.GPIO17, S1.ENA
  N3: 부품1.GPIO22, S1.IN2
  N4: 부품1.GPIO13, hc-sr3.Trig
  VCC: 부품1.+5V, hc-sr1.VCC, hc-sr2.VCC, hc-sr3.VCC, R1.Pin_0, S1.5V
  N5: 부품1.GPIO18, S1.ENB
  N6: 부품1.GPIO23, S1.IN3
  N7: 부품1.GPIO25, S1.IN4
  N8: 부품1.GPIO12, S1.IN1
  N9: 부품1.GPIO16, hc-sr2.Echo
  N10: 부품1.GPIO20, R3.Pin_0
  N11: 부품1.GPIO21, R5.Pin_0
  N12: hc-sr1.Echo, R5.Pin_1, R6.Pin_0
  N13: hc-sr2.Trig, R3.Pin_1, R4.Pin_0
  N14: hc-sr3.Echo, R1.Pin_1, R2.Pin_0
  N15: S1.12V, VCC1.+
  N16: S1.M1-01, M3.pin_2
  N17: S1.M1-02, M3.pin_1
  N18: S1.M2-01, M2.pin_2
  N19: S1.M2-02, M2.pin_1

custom parts:
  Adafruit T-Cobbler Plus: The Raspberry Pi has landed on the Maker World like a 40-GPIO pinned, quad-USB ported, credit card sized bomb of DIY joy. And while you can use most of our great Model B accessories by hooking up our downgrade cable, its probably a good time to upgrade your set up and accessorize using all of the 40 pins. That's why we now carry the Assembled Adafruit Pi T-Cobbler Plus - Breakout + Cable for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
  H-Bridge with L298N: h-bridge
